# Fritzing sketch lora-esp8266-wiring (saved by Fritzing 0.9.3b)

parts:
  WeMos_D1_Mini2 = WeMos D1 Mini
  Part1 = Adafruit RFM9x LoRa Radio [part_number="Adafruit #3072 and #3073"]

nets:
  3V3: WeMos_D1_Mini2.3V3, Part1.VIN
  N1: WeMos_D1_Mini2.D0, Part1.RST
  N2: WeMos_D1_Mini2.D1, Part1.DIO0
  N3: WeMos_D1_Mini2.D5, Part1.SCK
  N4: WeMos_D1_Mini2.D6, Part1.MISO
  N5: WeMos_D1_Mini2.D7, Part1.MOSI
  N6: WeMos_D1_Mini2.D8, Part1.CS
  N7: WeMos_D1_Mini2.G, Part1.GND

custom parts:
  Adafruit RFM9x LoRa Radio: Sending data over long distances is like magic, and now you can be a magician with this range of powerful and easy-to-use radio modules. Sure, sometimes you want to talk to a computer (a good time to use WiFi) or perhaps communicate with a Phone (choose Bluetooth Low Energy!) but what if you want to send data very far? Most WiFi, Bluetooth, Zigbee and other wireless chipsets use 2.4GHz, which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
