# Fritzing sketch neo6m-esp8266-wiring (saved by Fritzing 0.9.3b)

parts:
  WeMos_D1_Mini2 = WeMos D1 Mini
  Part2 = Adafruit Ultimate GPS v3 [part_number="Adafruit #746"]

nets:
  3V3: WeMos_D1_Mini2.3V3, Part2.VIN
  N1: WeMos_D1_Mini2.D2, Part2.TX
  N2: WeMos_D1_Mini2.D3, Part2.RX
  N3: WeMos_D1_Mini2.G, Part2.GND

custom parts:
  Adafruit Ultimate GPS v3: We carry a few different GPS modules here in the Adafruit shop, but none that satisfied our every desire - that's why we designed this little GPS breakout board. We believe this is the Ultimate GPS module, so we named it that. It's got everything you want and more: -165 dBm sensitivity, 10 Hz updates, 66 channels 5V friendly design and only 20mA current draw Breadboard friendly + two mounting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
